// Logisim project LAB3(a).circ as structural Verilog: 1 circuit, main circuit main
module main (
  input  in_1,
  input  B,
  output SUM,
  output CARRY
);

  xor xor_1 (SUM, in_1, B);
  and and_1 (CARRY, in_1, B);

  // Notes on the sheet:
  //   A
  //   SUM
  //   A
  //   B
  //   0
  //   0
  //   0
  //   1
  //   0
  //   1
  //   1
  //   0
  //   1
  //   0
  //   1
  //   1
  //   CARRY
  //   0
  //   0
  //   0
  //   1
endmodule
