// Logisim project LAB5.circ as structural Verilog: 1 circuit, main circuit main
module main (
  input  G4,
  input  G3,
  input  G2,
  input  G1,
  output B4,
  output B3,
  output B2,
  output B1
);

  xor xor_1 (B3, G4, G3);
  xor xor_2 (B2, B3, G2);
  xor xor_3 (B1, B2, G1);

  assign B4 = G4;
endmodule
